# Fritzing sketch Atmel386P_ESP8266 (saved by Fritzing 0.9.3b)
circuit board: 7.7831cm x 6.71824cm

parts:
  Part1 = Arduino Pro Mini v13
  Espessif_Serial_Wifi_Modul_1 = ESP8266 ESP01 [part_number=ESP8266 package=THT]
  (+)_Positive_IN = male pin header, 3 pins [form="♂ (male)"]
  (-)_Negative_IN = male pin header, 3 pins [form="♂ (male)"]
  A1_Header = male pin header, 3 pins [form="♂ (male)"]
  A0_Header = male pin header, 3 pins [form="♂ (male)"]
  I2C_Header = male pin header, 4 pins [form="♂ (male)"]
  LED_STATION_CONFIG_INIT_ERROR_6 = LEDs [package=led10mm]
  LED_PUBLISH_ERROR_5 = LEDs [package=led10mm]
  ED_MQTT_INIT_ERROR_4 = LEDs [package=led10mm]
  LED_WIFI_INIT_ERROR_3 = LEDs [package=led10mm]
  LED_STATION_INIT_ERROR_PIN_2 = LEDs [package=led10mm]
  R1 = Resistor [tolerance=±5% resistance=220 package=THT]
  R2 = Resistor [tolerance=±5% resistance=220 package=THT]
  R3 = Resistor [tolerance=±5% resistance=220 package=THT]
  R4 = Resistor [tolerance=±5% resistance=220 package=THT]
  R5 = Resistor [tolerance=±5% resistance=220 package=THT]
  R6 = Resistor [tolerance=±5% resistance=220 package=THT]
  R7 = Resistor [tolerance=±5% resistance=220 package=THT]
  R8 = Resistor [tolerance=±5% resistance=220 package=THT]

nets:
  N1: Part1.D0/TX, Espessif_Serial_Wifi_Modul_1.RXD
  N2: Part1.D1/RX, Espessif_Serial_Wifi_Modul_1.TXD
  N3: Part1.VCC, (+)_Positive_IN.pin3, A1_Header.pin2, A0_Header.pin2, I2C_Header.pin2, R6.Pin_1, R7.Pin_1, R8.Pin_1
  GND: Part1.GND, Espessif_Serial_Wifi_Modul_1.GND, (-)_Negative_IN.pin1, A1_Header.pin1, A0_Header.pin1, I2C_Header.pin1, LED_STATION_CONFIG_INIT_ERROR_6.C, LED_PUBLISH_ERROR_5.C, ED_MQTT_INIT_ERROR_4.C, LED_WIFI_INIT_ERROR_3.C, LED_STATION_INIT_ERROR_PIN_2.C
  N4: Part1.A1, A1_Header.pin3
  N5: Part1.A0, A0_Header.pin3
  N6: Part1.D11_PWM/MOSI, Espessif_Serial_Wifi_Modul_1.CH_PD
  N7: Part1.D10_PWM/SS, Espessif_Serial_Wifi_Modul_1.VCC
  N8: Part1.D8, I2C_Header.pin3
  N9: Part1.D7, I2C_Header.pin4
  N10: Part1.D6_PWM, R3.Pin_1
  N11: Part1.D5_PWM, R5.Pin_1
  N12: Part1.D4, R4.Pin_1
  N13: Part1.D3_PWM, R2.Pin_1
  N14: Part1.D2, R1.Pin_1
  N15: Espessif_Serial_Wifi_Modul_1.GPIO16, R8.Pin_0
  N16: Espessif_Serial_Wifi_Modul_1.GPIO00, R6.Pin_0
  N17: Espessif_Serial_Wifi_Modul_1.GPIO02, R7.Pin_0
  N18: LED_STATION_CONFIG_INIT_ERROR_6.A, R3.Pin_0
  N19: LED_PUBLISH_ERROR_5.A, R5.Pin_0
  N20: ED_MQTT_INIT_ERROR_4.A, R4.Pin_0
  N21: LED_WIFI_INIT_ERROR_3.A, R2.Pin_0
  N22: LED_STATION_INIT_ERROR_PIN_2.A, R1.Pin_0

custom parts:
  ESP8266 ESP01: Generic WiFi Module based on the ESP8266 with onboard PCB antenna and UART communications
